# Fritzing sketch mcu_assignment2 (saved by Fritzing 0.9.9b)
breadboards: 1

parts:
  U1 = NodeMCU V1.0
  Mod1 = KY-026 Flame Sensor Module [package="Breakout board"]
  Mod2 = KY-015 Temperature & Humidity Sensor Module [package="Breakout board"]
  LED1 = smd LED [color="Red (633nm)" package="0603 [SMD]"]
  LED2 = smd LED [color="Red (633nm)" package="0603 [SMD]"]
  R1 = Resistor [tolerance=±5% power=0.25 resistance=220 package=THT]
  R2 = Resistor [tolerance=±5% power=0.25 resistance=220 package=THT]

nets:
  N1: U1.D0, LED2.anode
  N2: U1.D3, Mod2.Vin
  N3: U1.D8, LED1.anode
  N4: U1.A0, Mod1.A0
  N5: Mod1.G, Mod2.-, R1.Pin_0, R2.Pin_0
  N6: Mod1.+, Mod2.S
  N7: LED1.cathode, R2.Pin_1
  N8: LED2.cathode, R1.Pin_1

custom parts:
  NodeMCU V1.0: ESP8266 based NodeMCU
  KY-026 Flame Sensor Module: KY-026 Flame Sensor Module reacts in the presence of fire.
  KY-015 Temperature & Humidity Sensor Module: KY-015 temperature and humidity sensor module, provides a low-latency serial interface to measure humidity and temperature.
