# Fritzing sketch mkr_assignment2 (saved by Fritzing 0.9.9b)
breadboards: 1

parts:
  Mod1 = KY-026 Flame Sensor Module [package="Breakout board"]
  Mod2 = KY-032 IR Obstacle Avoidance Sensor Module [package="Breakout board"]
  Mod3 = KY-004 Key Switch Module [package="Breakout board"]
  Componente1 = Arduino MKR1000
  R1 = Resistor [tolerance=±5% power=0.25 resistance=220 package=THT]
  LED2 = smd LED [color="Red (633nm)" package="0603 [SMD]"]
  LED3 = smd LED [color="Red (633nm)" package="0603 [SMD]"]
  LED4 = smd LED [color="Red (633nm)" package="0603 [SMD]"]
  LED5 = smd LED [color="Red (633nm)" package="0603 [SMD]"]
  R2 = Resistor [tolerance=±5% power=0.25 resistance=220 package=THT]
  R3 = Resistor [tolerance=±5% power=0.25 resistance=220 package=THT]
  R4 = Resistor [tolerance=±5% power=0.25 resistance=220 package=THT]
  R5 = Resistor [tolerance=±5% power=0.25 resistance=220 package=THT]
  LED1 = smd LED [color="Red (633nm)" package="0603 [SMD]"]

nets:
  N1: Mod1.A0, Componente1.A0/DAC0
  N2: Mod1.G, Mod2.GND, Mod3.-, R1.Pin_1, R2.Pin_1, R3.Pin_1, R4.Pin_1, R5.Pin_1
  N3: Mod1.+, Mod2.+, Mod3.Vin
  N4: Mod2.out, Componente1.D7
  N5: Mod3.S, Componente1.D6
  N6: Componente1.D2_PWM, LED3.anode
  N7: Componente1.D3_PWM, LED5.anode
  N8: Componente1.D4_PWM, LED4.anode
  N9: Componente1.D0, LED2.anode
  N10: Componente1.D1, LED1.anode
  N11: R1.Pin_0, LED3.cathode
  N12: LED2.cathode, R4.Pin_0
  N13: LED4.cathode, R2.Pin_0
  N14: LED5.cathode, R3.Pin_0
  N15: R5.Pin_0, LED1.cathode

custom parts:
  KY-026 Flame Sensor Module: KY-026 Flame Sensor Module reacts in the presence of fire.
  KY-032 IR Obstacle Avoidance Sensor Module: KY-032 Infrared Obstacle Avoidance Sensor. Distance-adjustable, infrared proximity sensor designed for wheeled robots. Also known as AD-032.
  KY-004 Key Switch Module: Arduino Key Switch Module Keyes KY-004 is a push button that will output a high signal when pressed.
  Arduino MKR1000: MKR1000 is a powerful board that combines the functionality of the Zero and the Wi-Fi Shield. It is the ideal solution for makers wanting to design IoT projects with minimal previous experience in networking
