# Fritzing sketch assignment1_mcu (saved by Fritzing 0.9.9b)
breadboards: 1

parts:
  U1 = NodeMCU V1.0
  Mod1 = KY-015 Temperature & Humidity Sensor Module [package="Breakout board"]
  KY-1 = Keyes Photo Resistor Sensor [package=THT]
  Mod2 = KY-004 Key Switch Module [package="Breakout board"]
  Mod3 = KY-004 Key Switch Module [package="Breakout board"]
  LED3 = LED - 3mm [color="Red (633nm)" current=0.030 package="3 mm [THT]"]
  LED4 = LED - 3mm [color="Red (633nm)" current=0.030 package="3 mm [THT]"]
  R1 = Resistor [tolerance=±5% resistance=220 package="1206 [SMD]"]
  R2 = Resistor [tolerance=±5% resistance=220 package="1206 [SMD]"]

nets:
  N1: U1.D0, Mod3.S
  N2: U1.D1, Mod2.S
  N3: U1.D3, KY-1.signal
  N4: U1.GND, Mod1.S, KY-1.ground, Mod2.-, Mod3.-, R1.Pin_1, R2.Pin_1
  N5: U1.D5, LED3.anode
  N6: U1.D6, LED4.anode
  VIN: U1.SD2, Mod1.-, KY-1.power, Mod2.Vin, Mod3.Vin
  N7: U1.A0, Mod1.Vin
  N8: LED3.cathode, R2.Pin_0
  N9: LED4.cathode, R1.Pin_0

custom parts:
  NodeMCU V1.0: ESP8266 based NodeMCU
  KY-015 Temperature & Humidity Sensor Module: KY-015 temperature and humidity sensor module, provides a low-latency serial interface to measure humidity and temperature.
  Keyes Photo Resistor Sensor: Keyes Photo Resistor Sensor Module for Arduino.
  KY-004 Key Switch Module: Arduino Key Switch Module Keyes KY-004 is a push button that will output a high signal when pressed.
