# Fritzing sketch iot_a1 (saved by Fritzing 0.9.9b)

parts:
  M1 = MKR Connector Carrier V3.0 [package=THT]
  Componente1 = Arduino MKR1000  # not connected
  Grove_LED_Red1 = Grove LED Red
  Grove_LED_Red2 = Grove LED Red
  Grove_LED_Red3 = Grove LED Red
  Grove_LED_Red4 = Grove LED Red
  Grove3 = Grove OLED 128x96

nets:
  GND: M1.GND, Grove_LED_Red1.GND, Grove_LED_Red2.GND, Grove_LED_Red3.GND, Grove_LED_Red4.GND, Grove3.GND
  5V: M1.5V, M1.+5V, Grove_LED_Red1.NC2, Grove_LED_Red2.NC2, Grove_LED_Red3.NC2, Grove_LED_Red4.NC2, Grove3.VCC
  N1: M1.SCL5, Grove3.SCL
  N2: M1.SDA5, Grove3.SDA
  N3: M1.I/O3, Grove_LED_Red4.SIG
  N4: M1.NC#73, Grove_LED_Red4.NC1
  N5: M1.I/O2, Grove_LED_Red3.SIG
  N6: M1.NC#77, Grove_LED_Red3.NC1
  N7: M1.I/O1, Grove_LED_Red2.SIG
  N8: M1.NC#81, Grove_LED_Red2.NC1
  N9: M1.I/O0, Grove_LED_Red1.SIG
  N10: M1.NC#85, Grove_LED_Red1.NC1

custom parts:
  MKR Connector Carrier V3.0: The Arduino MKR CONNECTOR CARRIER provides Seeed Studio's Grove connectors to your MKR board.
  Arduino MKR1000: MKR1000 is a powerful board that combines the functionality of the Zero and the Wi-Fi Shield. It is the ideal solution for makers wanting to design IoT projects with minimal previous experience in networking
  Grove LED Red: LED red, Grove connector.
